# Fritzing sketch robotarm_circuit (saved by Fritzing 0.9.3b)
breadboards: 1

parts:
  PWM1 = PCA9685 16x12-bit PWM Breakout
  esp1 = ESP32 DevKitc V4
  J1 = Basic Servo
  J2 = Basic Servo
  J3 = Basic Servo
  J4 = Basic Servo
  LED1 = LED - 5mm [color="Red (633nm)" package="5 mm [THT]"]
  LED2 = LED - 5mm [color="Yellow (595nm)" package="5 mm [THT]"]
  LED3 = LED - 5mm [color="Green (565nm)" package="5 mm [THT]"]
  JACK1 = 2.1mm Barrel Jack with Terminal Block
  JP1 = Header 2 [package=r_sw_th]
  R1 = Resistor [tolerance=±5% resistance=100 package="0402 [SMD]"]
  R2 = Resistor [tolerance=±5% resistance=100 package="0402 [SMD]"]
  R3 = Resistor [tolerance=±5% resistance=100 package="0402 [SMD]"]

nets:
  N1: PWM1.no_name_yet#0, J3.pulse
  N2: PWM1.no_name_yet#1, J4.pulse
  N3: PWM1.no_name_yet#2, J2.pulse
  N4: PWM1.no_name_yet#3, J1.pulse
  VCC: PWM1.no_name_yet#100, PWM1.no_name_yet#101, PWM1.no_name_yet#102, PWM1.no_name_yet#103, PWM1.no_name_yet#706, esp1.5V, J1.vcc, J2.vcc, J3.vcc, J4.vcc, JACK1.POS
  GND: PWM1.no_name_yet#601, PWM1.no_name_yet#701, PWM1.no_name_yet#1000, PWM1.no_name_yet#1001, PWM1.no_name_yet#1002, PWM1.no_name_yet#1003, esp1.GND#18, J1.gnd, J2.gnd, J3.gnd, J4.gnd, JACK1.NEG
  N5: PWM1.no_name_yet#603, esp1.IO22
  N6: PWM1.no_name_yet#604, esp1.IO21
  N7: esp1.IO34, JP1.2
  N8: esp1.IO33, R3.Pin_0
  N9: esp1.IO25, R2.Pin_0
  N10: esp1.IO27, R1.Pin_0
  N11: esp1.GND#32, LED1.anode, LED2.cathode, LED3.cathode, JP1.1

notes:
  rocker switch and led connections are arbitrary, change them as u wish in code & irl

custom parts:
  ESP32 DevKitc V4: ESP32-DevKitC board with ESP32-WROOM-32 module. ESP32-DevKitC V4 is a small-sized ESP32-based development board produced by Espressif. Most of the pins on the ESP module are broken out to the pin headers on the board. The pins D0, D1, D2, D3, CMD and CLK are used internally for communication between ESP32 and SPI flash memory. They are grouped on both sides near the USB connector. Avoid using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
